# Fritzing sketch scrolling-game (saved by Fritzing 0.9.10b)
breadboards: 1

parts:
  Part1 = Arduino Uno (Rev3)
  LCD1 = LCD screen
  R1 = Resistor [tolerance=±5% power=0.25W resistance=220 package=THT]
  U1 = POT [knob_status=50% power=0.5W package=pot_alpha_rv16af-20]

nets:
  N1: Part1.D8, LCD1.RS
  N2: Part1.D9_PWM, LCD1.E
  GND: Part1.GND, LCD1.VSS, LCD1.R/W, LCD1.LED-, U1.A
  N3: Part1.D4, LCD1.DB4
  N4: Part1.D5_PWM, LCD1.DB5
  N5: Part1.D6_PWM, LCD1.DB6
  N6: Part1.D7, LCD1.DB7
  5V: Part1.5V, LCD1.VDD, R1.Pin_0, U1.E
  N7: LCD1.V0, U1.S
  N8: LCD1.LED+, R1.Pin_1
