# Fritzing sketch LCD (saved by Fritzing 1.0.0d)
stripboards: 1

parts:
  LCD1 = LCD screen  # not connected
  J1 = female pin header, 16 pins [form="♀ (female)"]
  PWR = male pin header, 2 pins [form="♂ (male)"]
  RS = male pin header, 1 pin [form="♂ (male)"]
  Data_Pins = male pin header, 4 pins [form="♂ (male)"]
  EN = male pin header, 1 pin [form="♂ (male)"]
  R1 = Rotary Potentiometer (Large) [maximum_resistance=10kΩ knob_status=50% power=0.25W package=THT]

nets:
  N1: J1.pin1, J1.pin5, J1.pin16, PWR.pin1, R1.leg2
  N2: J1.pin2, J1.pin15, PWR.pin2, R1.leg1
  N3: J1.pin3, R1.wiper
  N4: J1.pin4, RS.pin1
  N5: J1.pin6, EN.pin1
  N6: J1.pin11, Data_Pins.pin1
  N7: J1.pin12, Data_Pins.pin2
  N8: J1.pin13, Data_Pins.pin3
  N9: J1.pin14, Data_Pins.pin4
