# Fritzing sketch adc (saved by Fritzing 0.9.10b)
breadboards: 1

parts:
  J1 = STM32 Nucleo boards
  R1 = Rotary Potentiometer (Large) [maximum_resistance=100kΩ knob_status=50% power=0.5W package=THT]

nets:
  N1: J1.A0, R1.wiper
  N2: J1.3V3, R1.leg2
  N3: J1.GND, R1.leg1
