# Fritzing sketch pwm (saved by Fritzing 1.0.0d)
breadboards: 1

parts:
  J1 = STM32 Nucleo boards
  P1 = Multimeter straight red probe
  P2 = Multimeter straight black probe

nets:
  N1: J1.GND, P2.Probe_tip
  N2: J1.PC13, P1.Probe_tip

notes:
  PWM Output
