# Fritzing sketch scrolling-game (saved by Fritzing 1.0.0d)
breadboards: 1

parts:
  LCD1 = LCD screen
  R1 = Resistor [tolerance=±5% power=0.25W resistance=220 package=THT]
  U1 = POT [knob_status=50% power=0.5W package=pot_alpha_rv16af-20]
  J1 = STM32 Nucleo boards

nets:
  VSS: LCD1.VSS, LCD1.R/W, LCD1.LED-, U1.A, J1.GND
  N1: LCD1.VDD, R1.Pin_0, U1.E
  N2: LCD1.V0, U1.S
  N3: LCD1.RS, J1.D8
  N4: LCD1.DB4, J1.D4
  N5: LCD1.DB5, J1.D5_PWM
  N6: LCD1.DB6, J1.D6_PWM
  N7: LCD1.DB7, J1.D7
  N8: LCD1.LED+, R1.Pin_1
